// Logisim project StdNum.circ as structural Verilog: 1 circuit, main circuit main
module main (
  input  in_1,
  input  in_2,
  input  in_3,
  input  in_4,
  input  in_5,
  input  in_6,
  input  in_7,
  input  in_8,
  input  in_9,
  input  in_10,
  input  in_11,
  input  in_12,
  input  in_13,
  input  in_14,
  input  in_15,
  input  in_16,
  input  in_17,
  input  in_18,
  input  in_19,
  input  in_20,
  input  in_21,
  input  in_22,
  input  in_23,
  input  in_24,
  input  in_25,
  input  in_26,
  input  in_27,
  input  in_28,
  input  in_29,
  input  in_30,
  input  in_31,
  input  in_32,
  input  in_33,
  input  in_34,
  input  in_35,
  input  in_36,
  input  in_37,
  input  in_38,
  input  in_39,
  input  in_40,
  input  in_41,
  input  in_42,
  input  in_43,
  input  in_44,
  input  in_45,
  input  in_46,
  input  in_47,
  input  in_48,
  input  in_49,
  input  in_50,
  input  in_51,
  input  in_52,
  input  in_53,
  input  in_54,
  input  in_55,
  input  in_56,
  input  in_57,
  input  in_58,
  input  in_59,
  input  in_60,
  input  in_61,
  input  in_62,
  input  in_63,
  input  in_64,
  input  in_65,
  input  in_66,
  input  in_67,
  input  in_68,
  input  in_69,
  input  in_70,
  input  in_71,
  input  in_72,
  input  in_73,
  input  in_74,
  input  in_75,
  input  in_76,
  input  in_77,
  input  in_78,
  input  in_79,
  input  in_80
);

  _7_Segment_Display u_7_segment_display_1 (
    .g(in_21), .f(in_1), .a(in_2), .b(in_22), .e(in_61), .d(in_41), .c(in_42), .dp(in_62));
  _7_Segment_Display u_7_segment_display_2 (
    .g(in_23), .f(in_3), .a(in_4), .b(in_24), .e(in_63), .d(in_43), .c(in_44), .dp(in_64));
  _7_Segment_Display u_7_segment_display_3 (
    .g(in_25), .f(in_5), .a(in_6), .b(in_26), .e(in_65), .d(in_45), .c(in_46), .dp(in_66));
  _7_Segment_Display u_7_segment_display_4 (
    .g(in_27), .f(in_7), .a(in_8), .b(in_28), .e(in_67), .d(in_47), .c(in_48), .dp(in_68));
  _7_Segment_Display u_7_segment_display_5 (
    .g(in_29), .f(in_9), .a(in_10), .b(in_30), .e(in_69), .d(in_49), .c(in_50), .dp(in_70));
  _7_Segment_Display u_7_segment_display_6 (
    .g(in_31), .f(in_11), .a(in_12), .b(in_32), .e(in_71), .d(in_51), .c(in_52), .dp(in_72));
  _7_Segment_Display u_7_segment_display_7 (
    .g(in_33), .f(in_13), .a(in_14), .b(in_34), .e(in_73), .d(in_53), .c(in_54), .dp(in_74));
  _7_Segment_Display u_7_segment_display_8 (
    .g(in_35), .f(in_15), .a(in_16), .b(in_36), .e(in_75), .d(in_55), .c(in_56), .dp(in_76));
  _7_Segment_Display u_7_segment_display_9 (
    .g(in_37), .f(in_17), .a(in_18), .b(in_38), .e(in_77), .d(in_57), .c(in_58), .dp(in_78));
  _7_Segment_Display u_7_segment_display_10 (
    .g(in_39), .f(in_19), .a(in_20), .b(in_40), .e(in_79), .d(in_59), .c(in_60), .dp(in_80));
endmodule
