// Logisim project Name.circ as structural Verilog: 1 circuit, main circuit main
module main (
);

  DotMatrix #(.inputtype("row"), .matrixcols(16), .matrixrows(16), .dotshape("circle")) dotmatrix_1 (
    .row0(16'h80), .row1(16'h80), .row2(16'h3ffc), .row3(16'h1c0), .row4(16'h3e0), .row5(16'h1ebc),
    .row6(16'h2082), .row7({16{1'b0}}), .row8(16'h3c0), .row9(16'h40), .row10(16'h3f8), .row11(16'h1fc0),
    .row12(16'h40), .row13(16'h240), .row14(16'h340), .row15(16'h1c0));
  DotMatrix #(.inputtype("row"), .matrixcols(16), .matrixrows(16), .dotshape("circle")) dotmatrix_2 (
    .row0({16{1'b0}}), .row1(16'h40), .row2(16'h2048), .row3(16'h23fc), .row4(16'h2040), .row5(16'h23fc),
    .row6(16'hfa44), .row7(16'h22e4), .row8(16'h2244), .row9(16'h22e4), .row10(16'h2008), .row11(16'h23fc),
    .row12(16'h2008), .row13(16'h2088), .row14(16'h38), .row15({16{1'b0}}));
  DotMatrix #(.inputtype("row"), .matrixcols(16), .matrixrows(16), .dotshape("circle")) dotmatrix_3 (
    .row0({16{1'b0}}), .row1(16'h4048), .row2(16'h60), .row3(16'h20), .row4(16'he3f8), .row5(16'h2230),
    .row6(16'h2210), .row7(16'h221a), .row8(16'h220c), .row9(16'h23cc), .row10(16'h224c), .row11(16'h22de),
    .row12(16'h26f3), .row13(16'h3420), .row14({16{1'b0}}), .row15({16{1'b0}}));
endmodule
