// Logisim project Q2&4.circ as structural Verilog
module \非门  (
  input  in_1,
  output out_2
);

  Transistor transistor_1 (.in(1'b1), .out(out_2), .gate(in_1));
  Transistor #(.\type ("n")) transistor_2 (.in(1'b0), .out(out_2), .gate(in_1));
endmodule

module \与门  (
  input  in_1,
  input  in_2,
  output out_3
);

  wire transistor_2_out;

  Transistor transistor_1 (.in(1'b0), .out(out_3), .gate(in_2));
  Transistor #(.\type ("n")) transistor_2 (.in(1'b1), .out(transistor_2_out), .gate(in_1));
  Transistor #(.\type ("n")) transistor_3 (.in(transistor_2_out), .out(out_3), .gate(in_2));
  Transistor transistor_4 (.in(1'b0), .out(out_3), .gate(in_1));
endmodule

module \或门  (
  input  in_1,
  input  in_2,
  output out_3
);

  wire transistor_4_out;

  Transistor #(.\type ("n")) transistor_1 (.in(1'b1), .out(out_3), .gate(in_1));
  Transistor #(.\type ("n")) transistor_2 (.in(1'b1), .out(out_3), .gate(in_2));
  Transistor transistor_3 (.in(transistor_4_out), .out(out_3), .gate(in_2));
  Transistor transistor_4 (.in(1'b0), .out(transistor_4_out), .gate(in_1));
endmodule

module \_2选1  (
  input  in_1,
  input  in_2,
  input  in_3,
  output out_4
);

  wire \与门_1_out_3 , \与门_2_out_3 , \非门_1_out_2 ;

  \非门  \u_非门_1  (.in_1(in_2), .out_2(\非门_1_out_2 ));
  \与门  \u_与门_1  (.in_1(in_1), .in_2(\非门_1_out_2 ), .out_3(\与门_1_out_3 ));
  \与门  \u_与门_2  (.in_1(in_2), .in_2(in_3), .out_3(\与门_2_out_3 ));
  \或门  \u_或门_1  (.in_1(\与门_1_out_3 ), .in_2(\与门_2_out_3 ), .out_3(out_4));
endmodule

module \四选一  (
  input  [1:0] in_1,
  input  [1:0] in_2,
  input  [1:0] in_3,
  input  [1:0] in_4,
  input  in_5,
  input  in_6,
  output [1:0] out_7
);

  wire \与门_1_out_3 , \与门_2_out_3 , \与门_3_out_3 , \与门_4_out_3 , \与门_5_out_3 , \与门_6_out_3 , \与门_7_out_3 ,
       \与门_8_out_3 , \与门_9_out_3 , \与门_10_out_3 , \与门_11_out_3 , \与门_12_out_3 , \与门_13_out_3 , \与门_14_out_3 ,
       \与门_15_out_3 , \与门_16_out_3 , \与门_17_out_3 , \与门_18_out_3 , \与门_19_out_3 , \与门_20_out_3 ,
       \与门_21_out_3 , \与门_22_out_3 , \非门_1_out_2 , \非门_2_out_2 , \非门_3_out_2 , \非门_4_out_2 , \非门_5_out_2 ,
       \非门_6_out_2 , \非门_7_out_2 , \非门_8_out_2 , \非门_9_out_2 , \非门_10_out_2 ;

  \非门  \u_非门_1  (.in_1(in_5), .out_2(\非门_1_out_2 ));
  \非门  \u_非门_2  (.in_1(in_6), .out_2(\非门_2_out_2 ));
  \与门  \u_与门_1  (.in_1(\非门_1_out_2 ), .in_2(\非门_2_out_2 ), .out_3(\与门_1_out_3 ));
  \与门  \u_与门_2  (.in_1(in_5), .in_2(\非门_2_out_2 ), .out_3(\与门_2_out_3 ));
  \与门  \u_与门_3  (.in_1(\非门_1_out_2 ), .in_2(in_6), .out_3(\与门_3_out_3 ));
  \与门  \u_与门_4  (.in_1(in_5), .in_2(in_6), .out_3(\与门_4_out_3 ));
  \与门  \u_与门_5  (.in_1(\非门_1_out_2 ), .in_2(\非门_2_out_2 ), .out_3(\与门_5_out_3 ));
  \与门  \u_与门_6  (.in_1(in_5), .in_2(\非门_2_out_2 ), .out_3(\与门_6_out_3 ));
  \与门  \u_与门_7  (.in_1(\非门_1_out_2 ), .in_2(in_6), .out_3(\与门_7_out_3 ));
  \与门  \u_与门_8  (.in_1(in_5), .in_2(in_6), .out_3(\与门_8_out_3 ));
  \与门  \u_与门_9  (.in_1(in_1[0]), .in_2(\与门_1_out_3 ), .out_3(\与门_9_out_3 ));
  \与门  \u_与门_10  (.in_1(in_2[0]), .in_2(\与门_2_out_3 ), .out_3(\与门_10_out_3 ));
  \与门  \u_与门_11  (.in_1(in_3[0]), .in_2(\与门_3_out_3 ), .out_3(\与门_11_out_3 ));
  \与门  \u_与门_12  (.in_1(in_4[0]), .in_2(\与门_4_out_3 ), .out_3(\与门_12_out_3 ));
  \与门  \u_与门_13  (.in_1(in_1[1]), .in_2(\与门_5_out_3 ), .out_3(\与门_13_out_3 ));
  \与门  \u_与门_14  (.in_1(in_2[1]), .in_2(\与门_6_out_3 ), .out_3(\与门_14_out_3 ));
  \与门  \u_与门_15  (.in_1(in_3[1]), .in_2(\与门_7_out_3 ), .out_3(\与门_15_out_3 ));
  \与门  \u_与门_16  (.in_1(in_4[1]), .in_2(\与门_8_out_3 ), .out_3(\与门_16_out_3 ));
  \非门  \u_非门_3  (.in_1(\与门_9_out_3 ), .out_2(\非门_3_out_2 ));
  \非门  \u_非门_4  (.in_1(\与门_10_out_3 ), .out_2(\非门_4_out_2 ));
  \非门  \u_非门_5  (.in_1(\与门_11_out_3 ), .out_2(\非门_5_out_2 ));
  \非门  \u_非门_6  (.in_1(\与门_12_out_3 ), .out_2(\非门_6_out_2 ));
  \非门  \u_非门_7  (.in_1(\与门_13_out_3 ), .out_2(\非门_7_out_2 ));
  \非门  \u_非门_8  (.in_1(\与门_14_out_3 ), .out_2(\非门_8_out_2 ));
  \非门  \u_非门_9  (.in_1(\与门_15_out_3 ), .out_2(\非门_9_out_2 ));
  \非门  \u_非门_10  (.in_1(\与门_16_out_3 ), .out_2(\非门_10_out_2 ));
  \与门  \u_与门_17  (.in_1(\非门_3_out_2 ), .in_2(\非门_4_out_2 ), .out_3(\与门_17_out_3 ));
  \与门  \u_与门_18  (.in_1(\非门_5_out_2 ), .in_2(\非门_6_out_2 ), .out_3(\与门_18_out_3 ));
  \与门  \u_与门_19  (.in_1(\非门_7_out_2 ), .in_2(\非门_8_out_2 ), .out_3(\与门_19_out_3 ));
  \与门  \u_与门_20  (.in_1(\非门_9_out_2 ), .in_2(\非门_10_out_2 ), .out_3(\与门_20_out_3 ));
  \与门  \u_与门_21  (.in_1(\与门_17_out_3 ), .in_2(\与门_18_out_3 ), .out_3(\与门_21_out_3 ));
  \非门  \u_非门_11  (.in_1(\与门_21_out_3 ), .out_2(out_7[0]));
  \与门  \u_与门_22  (.in_1(\与门_19_out_3 ), .in_2(\与门_20_out_3 ), .out_3(\与门_22_out_3 ));
  \非门  \u_非门_12  (.in_1(\与门_22_out_3 ), .out_2(out_7[1]));
endmodule
