// Logisim project Q1.circ as structural Verilog: 10 circuits, main circuit main
module main (
  input  Ci_1,
  input  Ai,
  input  Bi,
  output Si,
  output Ci
);

  wire and_1_out, and_2_out, and_3_out, and_4_out, and_5_out, and_6_out, and_7_out, not_1_out, not_2_out,
       not_3_out, not_4_out, not_5_out, not_6_out;

  not not_1 (not_1_out, Ci_1);
  not not_2 (not_2_out, Ai);
  not not_3 (not_3_out, Ci_1);
  not not_4 (not_4_out, Bi);
  not not_5 (not_5_out, Ai);
  not not_6 (not_6_out, Bi);
  and and_1 (and_1_out, Ai, Bi);
  and and_2 (and_2_out, Ci_1, Bi);
  and and_3 (and_3_out, Ci_1, Ai);
  and and_4 (and_4_out, not_1_out, not_2_out, Bi);
  and and_5 (and_5_out, not_3_out, Ai, not_4_out);
  and and_6 (and_6_out, Ci_1, not_5_out, not_6_out);
  and and_7 (and_7_out, Ci_1, Ai, Bi);
  or or_1 (Ci, and_1_out, and_2_out, and_3_out);
  or or_2 (Si, and_4_out, and_5_out, and_6_out, and_7_out);
endmodule

module Q2 (
  input  G1,
  input  G2,
  input  G3,
  input  A2,
  input  A1,
  input  A0,
  output Y7,
  output Y6,
  output Y5,
  output Y4,
  output Y3,
  output Y2,
  output Y1,
  output Y0
);

  wire not_1_out, not_2_out, not_3_out, not_4_out, not_5_out, not_6_out, not_7_out, not_8_out, not_9_out,
       not_10_out, not_11_out, not_12_out, not_13_out, not_14_out, not_15_out, not_16_out, not_17_out,
       not_18_out, not_19_out, not_20_out, not_21_out, not_22_out, not_23_out, not_24_out, not_25_out,
       not_26_out, not_27_out;

  not not_1 (not_1_out, G2);
  not not_2 (not_2_out, G3);
  not not_3 (not_3_out, G2);
  not not_4 (not_4_out, G3);
  not not_5 (not_5_out, A0);
  not not_6 (not_6_out, G2);
  not not_7 (not_7_out, G3);
  not not_8 (not_8_out, A1);
  not not_9 (not_9_out, G2);
  not not_10 (not_10_out, G3);
  not not_11 (not_11_out, A1);
  not not_12 (not_12_out, A0);
  not not_13 (not_13_out, G2);
  not not_14 (not_14_out, G3);
  not not_15 (not_15_out, A2);
  not not_16 (not_16_out, G2);
  not not_17 (not_17_out, G3);
  not not_18 (not_18_out, A2);
  not not_19 (not_19_out, A0);
  not not_20 (not_20_out, G2);
  not not_21 (not_21_out, G3);
  not not_22 (not_22_out, A2);
  not not_23 (not_23_out, A1);
  not not_24 (not_24_out, G2);
  not not_25 (not_25_out, G3);
  not not_26 (not_26_out, A2);
  not not_27 (not_27_out, A1);
  nand nand_1 (Y7, G1, not_1_out, not_2_out, A2, A1, A0);
  nand nand_2 (Y6, G1, not_3_out, not_4_out, A2, A1, not_5_out);
  nand nand_3 (Y5, G1, not_6_out, not_7_out, A2, not_8_out, A0);
  nand nand_4 (Y4, G1, not_9_out, not_10_out, A2, not_11_out, not_12_out);
  nand nand_5 (Y3, G1, not_13_out, not_14_out, not_15_out, A1, A0);
  nand nand_6 (Y2, G1, not_16_out, not_17_out, not_18_out, A1, not_19_out);
  nand nand_7 (Y1, G1, not_20_out, not_21_out, not_22_out, not_23_out, A0);
  nand nand_8 (Y0, G1, not_24_out, not_25_out, not_26_out, not_27_out, A0);
endmodule

module Q2test (
  input  G1,
  input  G2,
  input  G3,
  input  A2,
  input  A1,
  input  A0,
  output Y7,
  output Y6,
  output Y5,
  output Y4,
  output Y3,
  output Y2,
  output Y1,
  output Y0
);

  wire not_1_out, not_2_out, not_3_out, not_4_out, not_5_out, not_6_out, not_7_out, not_8_out, not_9_out,
       not_10_out, not_11_out, not_12_out, not_13_out, not_14_out, not_15_out, not_16_out, not_17_out,
       not_18_out, not_19_out, not_20_out, not_21_out, not_22_out, not_23_out, not_24_out, not_25_out,
       not_26_out, not_27_out;

  not not_1 (not_1_out, G2);
  not not_2 (not_2_out, G3);
  not not_3 (not_3_out, G2);
  not not_4 (not_4_out, G3);
  not not_5 (not_5_out, A0);
  not not_6 (not_6_out, G2);
  not not_7 (not_7_out, G3);
  not not_8 (not_8_out, A1);
  not not_9 (not_9_out, G2);
  not not_10 (not_10_out, G3);
  not not_11 (not_11_out, A1);
  not not_12 (not_12_out, A0);
  not not_13 (not_13_out, G2);
  not not_14 (not_14_out, G3);
  not not_15 (not_15_out, A2);
  not not_16 (not_16_out, G2);
  not not_17 (not_17_out, G3);
  not not_18 (not_18_out, A2);
  not not_19 (not_19_out, A0);
  not not_20 (not_20_out, G2);
  not not_21 (not_21_out, G3);
  not not_22 (not_22_out, A2);
  not not_23 (not_23_out, A1);
  not not_24 (not_24_out, G2);
  not not_25 (not_25_out, G3);
  not not_26 (not_26_out, A2);
  not not_27 (not_27_out, A1);
  nand nand_1 (Y7, G1, not_1_out, not_2_out, A2, A1, A0);
  nand nand_2 (Y6, G1, not_3_out, not_4_out, A2, A1, not_5_out);
  nand nand_3 (Y5, G1, not_6_out, not_7_out, A2, not_8_out, A0);
  nand nand_4 (Y4, G1, not_9_out, not_10_out, A2, not_11_out, not_12_out);
  nand nand_5 (Y3, G1, not_13_out, not_14_out, not_15_out, A1, A0);
  nand nand_6 (Y2, G1, not_16_out, not_17_out, not_18_out, A1, not_19_out);
  nand nand_7 (Y1, G1, not_20_out, not_21_out, not_22_out, not_23_out, A0);
  nand nand_8 (Y0, G1, not_24_out, not_25_out, not_26_out, not_27_out, A0);
endmodule

module Q2_test (
  input  G1,
  input  G2,
  input  G3,
  input  A2,
  input  A1,
  input  A0,
  output Y7,
  output Y6,
  output Y5,
  output Y4,
  output Y3,
  output Y2,
  output Y1,
  output Y0
);

  wire not_1_out, not_2_out, not_3_out, not_4_out, not_5_out, not_6_out, not_7_out, not_8_out, not_9_out,
       not_10_out, not_11_out, not_12_out, not_13_out, not_14_out, not_15_out, not_16_out, not_17_out,
       not_18_out, not_19_out, not_20_out, not_21_out, not_22_out, not_23_out, not_24_out, not_25_out,
       not_26_out, not_27_out;

  not not_1 (not_1_out, G2);
  not not_2 (not_2_out, G3);
  not not_3 (not_3_out, G1);
  not not_4 (not_4_out, A2);
  not not_5 (not_5_out, A1);
  not not_6 (not_6_out, G2);
  not not_7 (not_7_out, G3);
  not not_8 (not_8_out, A1);
  not not_9 (not_9_out, G2);
  not not_10 (not_10_out, G3);
  not not_11 (not_11_out, A1);
  not not_12 (not_12_out, A0);
  not not_13 (not_13_out, G2);
  not not_14 (not_14_out, G3);
  not not_15 (not_15_out, A2);
  not not_16 (not_16_out, G2);
  not not_17 (not_17_out, G3);
  not not_18 (not_18_out, A2);
  not not_19 (not_19_out, A0);
  not not_20 (not_20_out, G2);
  not not_21 (not_21_out, G3);
  not not_22 (not_22_out, A2);
  not not_23 (not_23_out, A1);
  not not_24 (not_24_out, G2);
  not not_25 (not_25_out, G3);
  not not_26 (not_26_out, A2);
  not not_27 (not_27_out, A1);
  nand nand_1 (Y7, G1, not_1_out, not_2_out, A2, A1, A0);
  or or_1 (Y6, not_3_out, not_4_out, not_5_out, A0, G3, G2);
  nand nand_2 (Y5, G1, not_6_out, not_7_out, A2, not_8_out, A0);
  nand nand_3 (Y4, G1, not_9_out, not_10_out, A2, not_11_out, not_12_out);
  nand nand_4 (Y3, G1, not_13_out, not_14_out, not_15_out, A1, A0);
  nand nand_5 (Y2, G1, not_16_out, not_17_out, not_18_out, A1, not_19_out);
  nand nand_6 (Y1, G1, not_20_out, not_21_out, not_22_out, not_23_out, A0);
  nand nand_7 (Y0, G1, not_24_out, not_25_out, not_26_out, not_27_out, A0);
endmodule

module Q2_test1 (
  input  G1,
  input  G2,
  input  G3,
  input  A2,
  input  A1,
  input  A0,
  output Y7,
  output Y6,
  output Y5,
  output Y4,
  output Y3,
  output Y2,
  output Y1,
  output Y0
);

  wire not_1_out, not_2_out, not_3_out, not_4_out, not_5_out, not_6_out, not_7_out, not_8_out, not_9_out,
       not_10_out, not_11_out, not_12_out, not_13_out, not_14_out, not_15_out, not_16_out, not_17_out,
       not_18_out, not_19_out, not_20_out, not_21_out, not_22_out, not_23_out, not_24_out, not_25_out,
       not_26_out, not_27_out, not_28_out, not_29_out;

  not not_1 (not_1_out, G1);
  not not_2 (not_2_out, A2);
  not not_3 (not_3_out, A1);
  not not_4 (not_4_out, A0);
  not not_5 (not_5_out, G1);
  not not_6 (not_6_out, A2);
  not not_7 (not_7_out, A1);
  not not_8 (not_8_out, G2);
  not not_9 (not_9_out, G3);
  not not_10 (not_10_out, A1);
  not not_11 (not_11_out, G2);
  not not_12 (not_12_out, G3);
  not not_13 (not_13_out, A1);
  not not_14 (not_14_out, A0);
  not not_15 (not_15_out, G2);
  not not_16 (not_16_out, G3);
  not not_17 (not_17_out, A2);
  not not_18 (not_18_out, G2);
  not not_19 (not_19_out, G3);
  not not_20 (not_20_out, A2);
  not not_21 (not_21_out, A0);
  not not_22 (not_22_out, G2);
  not not_23 (not_23_out, G3);
  not not_24 (not_24_out, A2);
  not not_25 (not_25_out, A1);
  not not_26 (not_26_out, G2);
  not not_27 (not_27_out, G3);
  not not_28 (not_28_out, A2);
  not not_29 (not_29_out, A1);
  or or_1 (Y7, not_1_out, G2, G3, not_2_out, not_3_out, not_4_out);
  or or_2 (Y6, not_5_out, not_6_out, not_7_out, A0, G3, G2);
  nand nand_1 (Y5, G1, not_8_out, not_9_out, A2, not_10_out, A0);
  nand nand_2 (Y4, G1, not_11_out, not_12_out, A2, not_13_out, not_14_out);
  nand nand_3 (Y3, G1, not_15_out, not_16_out, not_17_out, A1, A0);
  nand nand_4 (Y2, G1, not_18_out, not_19_out, not_20_out, A1, not_21_out);
  nand nand_5 (Y1, G1, not_22_out, not_23_out, not_24_out, not_25_out, A0);
  nand nand_6 (Y0, G1, not_26_out, not_27_out, not_28_out, not_29_out, A0);
endmodule

module Q3 (
  input  a,
  input  sel,
  input  b,
  output out
);

  wire and_1_out, and_2_out, not_1_out;

  not not_1 (not_1_out, sel);
  and and_1 (and_1_out, a, not_1_out);
  and and_2 (and_2_out, sel, b);
  or or_1 (out, and_1_out, and_2_out);
endmodule

module Q4 (
  input  in_1,
  input  in_2,
  input  in_3,
  input  in_4,
  input  in_5,
  input  in_6,
  output out_7
);

  wire q3_1_1_out_4, q3_1_2_out_4;

  Q3_1 q3_1_1 (.in_1(in_1), .in_2(in_6), .in_3(in_2), .out_4(q3_1_1_out_4));
  Q3_1 q3_1_2 (.in_1(in_3), .in_2(in_6), .in_3(in_4), .out_4(q3_1_2_out_4));
  Q3_1 q3_1_3 (.in_1(q3_1_1_out_4), .in_2(in_5), .in_3(q3_1_2_out_4), .out_4(out_7));
endmodule

module Q3_1 (
  input  in_1,
  input  in_2,
  input  in_3,
  output out_4
);

  wire and_1_out, and_2_out, not_1_out;

  not not_1 (not_1_out, in_2);
  and and_1 (and_1_out, in_1, not_1_out);
  and and_2 (and_2_out, in_2, in_3);
  or or_1 (out_4, and_1_out, and_2_out);
endmodule

module Q6 (
  input  a,
  input  b,
  input  c,
  output s1,
  output s2
);

  wire and_1_out, and_2_out, and_3_out, and_4_out, and_5_out, and_6_out, and_7_out, and_8_out, not_1_out,
       not_2_out, not_3_out, not_4_out, not_5_out, not_6_out, not_7_out, not_8_out, not_9_out, not_10_out,
       not_11_out, not_12_out;

  not not_1 (not_1_out, a);
  not not_2 (not_2_out, b);
  not not_3 (not_3_out, a);
  not not_4 (not_4_out, c);
  not not_5 (not_5_out, b);
  not not_6 (not_6_out, c);
  not not_7 (not_7_out, a);
  not not_8 (not_8_out, b);
  not not_9 (not_9_out, c);
  not not_10 (not_10_out, a);
  not not_11 (not_11_out, b);
  not not_12 (not_12_out, c);
  and and_1 (and_1_out, not_1_out, not_2_out, c);
  and and_2 (and_2_out, not_3_out, b, not_4_out);
  and and_3 (and_3_out, a, not_5_out, not_6_out);
  and and_4 (and_4_out, a, b, c);
  and and_5 (and_5_out, not_7_out, b, c);
  and and_6 (and_6_out, a, not_8_out, c);
  and and_7 (and_7_out, a, b, not_9_out);
  and and_8 (and_8_out, not_10_out, not_11_out, not_12_out);
  or or_1 (s2, and_5_out, and_6_out, and_7_out, and_8_out);
  or or_2 (s1, and_1_out, and_2_out, and_3_out, and_4_out);
endmodule

module q6_2 (
  input  a,
  input  b,
  input  c,
  output s1,
  output s2
);

  wire and_1_out, and_2_out, and_3_out, and_4_out, and_5_out, and_6_out, and_7_out, and_8_out, not_1_out,
       not_2_out, not_3_out, not_4_out, not_5_out, not_6_out, not_7_out, not_8_out, not_9_out, not_10_out,
       not_11_out, not_12_out;

  not not_1 (not_1_out, a);
  not not_2 (not_2_out, b);
  not not_3 (not_3_out, a);
  not not_4 (not_4_out, c);
  not not_5 (not_5_out, b);
  not not_6 (not_6_out, c);
  not not_7 (not_7_out, a);
  not not_8 (not_8_out, b);
  not not_9 (not_9_out, c);
  not not_10 (not_10_out, a);
  not not_11 (not_11_out, b);
  not not_12 (not_12_out, c);
  and and_1 (and_1_out, not_1_out, not_2_out, c);
  and and_2 (and_2_out, not_3_out, b, not_4_out);
  and and_3 (and_3_out, a, not_5_out, not_6_out);
  and and_4 (and_4_out, a, b, c);
  and and_5 (and_5_out, not_7_out, b, c);
  and and_6 (and_6_out, a, not_8_out, c);
  and and_7 (and_7_out, a, b, not_9_out);
  and and_8 (and_8_out, not_10_out, not_11_out, not_12_out);
  or or_1 (s1, and_1_out, and_2_out, and_3_out, and_4_out);
  or or_2 (s2, and_5_out, and_6_out, and_7_out, and_8_out);
endmodule
