// Logisim project q1.circ as structural Verilog: 21 circuits, main circuit Q1_SR_Latch
module Q1_SR_Latch (
  input  S,
  input  R,
  output Q,
  output nQ
);

  nand nand_1 (Q, ~S, nQ);  // NAND_Gate
  nand nand_2 (nQ, Q, ~R);  // NAND_Gate
endmodule

module D_Latch (
  input  D,
  input  CLK,
  output out_3,
  output out_4
);

  wire and_1_out, and_2_out, not_1_out;

  not not_1 (not_1_out, D);
  and and_1 (and_1_out, D, CLK);
  and and_2 (and_2_out, not_1_out, CLK);
  Q1_SR_Latch q1_sr_latch_1 (.S(and_1_out), .R(and_2_out), .Q(out_3), .nQ(out_4));
endmodule

module D_FF (
  input  D,
  input  CLK,
  output out_3,
  output out_4
);

  wire d_latch_1_out_3, not_1_out;

  not not_1 (not_1_out, CLK);
  D_Latch d_latch_1 (.D(D), .CLK(not_1_out), .out_3(d_latch_1_out_3));  // open: out_4
  D_Latch d_latch_2 (.D(d_latch_1_out_3), .CLK(CLK), .out_3(out_3), .out_4(out_4));
endmodule

module Q2_D_FF_P (
  input  D,
  input  nRST,
  output out_3,
  output out_4
);

  wire CLK_out, or_1_out;

  Clock CLK (.out(CLK_out));
  or or_1 (or_1_out, D, nRST);
  D_FF d_ff_1 (.D(or_1_out), .out_3(out_3), .out_4(out_4), .CLK(CLK_out));
endmodule

module Q3_D_FF_N (
  input  RST,
  input  D,
  output out_3
);

  wire clock_1_out, not_1_out, q3_d_latch_1_out_5;

  Clock clock_1 (.out(clock_1_out));
  not not_1 (not_1_out, clock_1_out);
  Q3_D_Latch q3_d_latch_1 (.RST(1'b0), .D(D), .out_5(q3_d_latch_1_out_5), .CLK(not_1_out));  // open: out_4
  Q3_D_Latch q3_d_latch_2 (.RST(RST), .D(q3_d_latch_1_out_5), .out_5(out_3), .CLK(clock_1_out));  // open: out_4
endmodule

module Q3_4bitCounter (
  input  in_1,
  output [3:0] out_2
);

  wire clock_1_out;
  wire [3:0] adder_1_out;

  Adder #(.width(4)) adder_1 (.a(out_2), .b(4'b0001), .out(adder_1_out), .cin(1'b0));  // open: cout
  Clock clock_1 (.out(clock_1_out));
  _4bitReg u_4bitreg_1 (.in_1(adder_1_out), .CLK(clock_1_out), .nRST(in_1), .out_4(out_2));
endmodule

module _4bitReg (
  input  [3:0] in_1,
  input  CLK,
  input  nRST,
  output [3:0] out_4
);

  wire and_1_out, and_2_out, and_3_out, and_4_out, not_1_out;

  and and_1 (and_1_out, not_1_out, in_1[3]);
  and and_2 (and_2_out, not_1_out, in_1[2]);
  and and_3 (and_3_out, not_1_out, in_1[1]);
  and and_4 (and_4_out, not_1_out, in_1[0]);
  not not_1 (not_1_out, nRST);
  Q3_D_FF_N q3_d_ff_n_1 (.D(and_1_out), .out_3(out_4[3]), .RST(nRST));
  Q3_D_FF_N q3_d_ff_n_2 (.D(and_2_out), .out_3(out_4[2]), .RST(nRST));
  Q3_D_FF_N q3_d_ff_n_3 (.D(and_3_out), .out_3(out_4[1]), .RST(nRST));
  Q3_D_FF_N q3_d_ff_n_4 (.D(and_4_out), .out_3(out_4[0]), .RST(nRST));
endmodule

module Q4Sel (
  input  [3:0] in_1,
  output [3:0] out_2
);

  wire and_1_out, and_2_out, not_1_out, not_2_out, not_3_out, not_4_out, not_5_out, not_6_out;

  not not_1 (not_1_out, in_1[2]);
  not not_2 (not_2_out, in_1[1]);
  not not_3 (not_3_out, in_1[0]);
  not not_4 (not_4_out, in_1[3]);
  not not_5 (not_5_out, in_1[2]);
  not not_6 (not_6_out, in_1[0]);
  and and_1 (and_1_out, not_1_out, not_2_out, not_3_out);
  and and_2 (and_2_out, not_4_out, not_5_out, not_6_out);
  or or_1 (out_2[3], and_1_out, in_1[3]);
  or or_2 (out_2[1], and_2_out, in_1[1]);

  assign {out_2[2], out_2[0]} = {in_1[2], in_1[0]};
endmodule

module Q4_0to9 (
  input  in_1,
  output [3:0] out_2
);

  wire clock_1_out, not_1_out;
  wire [3:0] n4bitreg_1_out_4, sel5_1_out_2, subtractor_1_out;

  Subtractor #(.width(4)) subtractor_1 (
    .a(sel5_1_out_2), .b(4'b0001), .out(subtractor_1_out), .bin(1'b0));  // open: bout
  Clock clock_1 (.out(clock_1_out));
  not not_1 (not_1_out, clock_1_out);
  SEL5 sel5_1 (.in_1(n4bitreg_1_out_4), .out_2(sel5_1_out_2));
  _4bitReg u_4bitreg_1 (.in_1(subtractor_1_out), .CLK(not_1_out), .nRST(in_1), .out_4(n4bitreg_1_out_4));
  SEL6 sel6_1 (.out_2(out_2), .in_1(n4bitreg_1_out_4));
endmodule

module Q5Sample (
  input  in_1,
  output [3:0] out_2
);

  wire clock_1_out, not_1_out;
  wire [3:0] n4bitreg_1_out_4, subtractor_1_out;

  Subtractor #(.width(4)) subtractor_1 (.a(out_2), .b(4'b0001), .out(subtractor_1_out), .bin(1'b0));  // open: bout
  Clock clock_1 (.out(clock_1_out));
  not not_1 (not_1_out, clock_1_out);
  SEL5 sel5_1 (.in_1(n4bitreg_1_out_4), .out_2(out_2));
  _4bitReg u_4bitreg_1 (.in_1(subtractor_1_out), .CLK(not_1_out), .nRST(in_1), .out_4(n4bitreg_1_out_4));
endmodule

module Q4Sel_2 (
  input  [3:0] in_1,
  output [3:0] out_2
);

  wire and_1_out, and_2_out, not_1_out, not_2_out, not_3_out, not_4_out, not_5_out, not_6_out;

  not not_1 (not_1_out, in_1[2]);
  not not_2 (not_2_out, in_1[1]);
  and and_1 (and_1_out, not_1_out, not_2_out, not_3_out);
  not not_3 (not_3_out, in_1[0]);
  not not_4 (not_4_out, in_1[3]);
  and and_2 (and_2_out, not_4_out, not_5_out, not_6_out);
  not not_5 (not_5_out, in_1[2]);
  not not_6 (not_6_out, in_1[1]);
  or or_1 (out_2[3], and_1_out, in_1[3]);
  or or_2 (out_2[0], and_2_out, in_1[0]);

  assign out_2[2:1] = in_1[2:1];
endmodule

module Q3_D_Latch (
  input  RST,
  input  CLK,
  input  D,
  output out_4,
  output out_5
);

  wire and_1_out, and_2_out, and_3_out, not_1_out, not_2_out, or_1_out;

  not not_1 (not_1_out, D);
  and and_1 (and_1_out, CLK, not_1_out);
  and and_2 (and_2_out, CLK, D);
  not not_2 (not_2_out, RST);
  or or_1 (or_1_out, RST, and_1_out);
  and and_3 (and_3_out, and_2_out, not_2_out);
  Q1_SR_Latch q1_sr_latch_1 (.S(or_1_out), .R(and_3_out), .Q(out_4), .nQ(out_5));
endmodule

module Q4SEL_3 (
  input  [3:0] in_1,
  output Y1,
  output Y2,
  output Y3,
  output Y4
);

  wire and_1_out, and_2_out, and_3_out, and_4_out, not_1_out, not_2_out, undriven, undriven_2;

  not not_1 (not_1_out, undriven_2);
  not not_2 (not_2_out, undriven);
  and and_1 (and_1_out, undriven, not_1_out);
  and and_2 (and_2_out, undriven, Y4);
  and and_3 (and_3_out, not_2_out, undriven_2);
  and and_4 (and_4_out, undriven_2, Y4);
  or or_1 (Y1, and_1_out, and_2_out);
  or or_2 (Y3, and_3_out, and_4_out);
endmodule

module Q4_SEL_4 (
  input  [3:0] in_1,
  output [3:0] out_2
);

  wire and_1_out, and_2_out, and_3_out, and_4_out, not_1_out, not_2_out;

  not not_1 (not_1_out, in_1[1]);
  not not_2 (not_2_out, in_1[3]);
  and and_1 (and_1_out, in_1[3], not_1_out);
  and and_2 (and_2_out, in_1[3], in_1[0]);
  and and_3 (and_3_out, not_2_out, in_1[1]);
  and and_4 (and_4_out, in_1[1], in_1[0]);
  or or_1 (out_2[3], and_1_out, and_2_out);
  or or_2 (out_2[1], and_3_out, and_4_out);

  assign {out_2[2], out_2[0]} = {in_1[2], in_1[0]};
endmodule

module sel4 (
  input  [3:0] in_1,
  output [3:0] out_2
);

  wire and_1_out, and_2_out, and_3_out, and_4_out, not_1_out, not_2_out;

  not not_1 (not_1_out, in_1[1]);
  not not_2 (not_2_out, in_1[3]);
  and and_1 (and_1_out, in_1[3], not_1_out);
  and and_2 (and_2_out, in_1[3], in_1[0]);
  and and_3 (and_3_out, not_2_out, in_1[1]);
  and and_4 (and_4_out, in_1[1], in_1[0]);
  or or_1 (out_2[3], and_1_out, and_2_out);
  or or_2 (out_2[1], and_3_out, and_4_out);

  assign {out_2[2], out_2[0]} = {in_1[2], in_1[0]};
endmodule

module SEL5 (
  input  [3:0] in_1,
  output [3:0] out_2
);

  wire and_2_out, and_3_out, not_1_out, not_2_out, not_3_out;

  not not_1 (not_1_out, in_1[3]);
  and and_1 (out_2[2], not_1_out, in_1[2]);
  not not_2 (not_2_out, in_1[3]);
  and and_2 (and_2_out, not_2_out, in_1[1]);
  not not_3 (not_3_out, in_1[2]);
  and and_3 (and_3_out, not_3_out, in_1[1]);
  or or_1 (out_2[1], and_2_out, and_3_out);

  assign {out_2[3], out_2[0]} = {in_1[3], in_1[0]};
endmodule

module SRLATCH (
  input  S,
  input  R,
  output Q,
  output nQ
);

  nor nor_1 (Q, S, nQ);
  nor nor_2 (nQ, Q, R);
endmodule

module D_FF_PPP (
  input  D,
  input  nRST,
  output out_3,
  output out_4
);

  wire and_1_out, CLK_out;

  Clock CLK (.out(CLK_out));
  and and_1 (and_1_out, D, nRST);
  D_FF d_ff_1 (.D(and_1_out), .out_3(out_3), .out_4(out_4), .CLK(CLK_out));
endmodule

module SEL6 (
  input  [3:0] in_1,
  output [3:0] out_2
);

  wire and_1_out, and_2_out, and_3_out, and_4_out, and_5_out, and_6_out, and_7_out, and_8_out, and_9_out,
       and_10_out, and_11_out, and_12_out, and_13_out, and_14_out, and_15_out, and_16_out, not_1_out,
       not_2_out, not_3_out, not_4_out, not_5_out, not_6_out, not_7_out, not_8_out, not_9_out, not_10_out,
       not_11_out, not_12_out, not_13_out, not_14_out, not_15_out, not_16_out, not_17_out, not_18_out,
       not_19_out, not_20_out, not_21_out, not_22_out;

  not not_1 (not_1_out, in_1[3]);
  not not_2 (not_2_out, in_1[2]);
  not not_3 (not_3_out, in_1[1]);
  not not_4 (not_4_out, in_1[0]);
  not not_5 (not_5_out, in_1[1]);
  not not_6 (not_6_out, in_1[3]);
  not not_7 (not_7_out, in_1[1]);
  not not_8 (not_8_out, in_1[0]);
  not not_9 (not_9_out, in_1[0]);
  not not_10 (not_10_out, in_1[3]);
  not not_11 (not_11_out, in_1[1]);
  not not_12 (not_12_out, in_1[0]);
  not not_13 (not_13_out, in_1[1]);
  and and_1 (and_1_out, not_1_out, not_2_out, not_3_out, not_4_out);
  and and_2 (and_2_out, in_1[3], in_1[0]);
  and and_3 (and_3_out, in_1[3], in_1[1]);
  and and_4 (and_4_out, in_1[3], in_1[2]);
  and and_5 (and_5_out, in_1[2], not_5_out, in_1[0]);
  and and_6 (and_6_out, not_6_out, in_1[2], in_1[1]);
  and and_7 (and_7_out, in_1[3], not_7_out, not_8_out);
  and and_8 (and_8_out, in_1[3], in_1[2], not_9_out);
  not not_14 (not_14_out, in_1[3]);
  and and_9 (and_9_out, not_14_out, in_1[1], in_1[0]);
  and and_10 (and_10_out, not_10_out, in_1[2], not_11_out, not_12_out);
  not not_15 (not_15_out, in_1[2]);
  and and_11 (and_11_out, in_1[3], not_15_out, not_16_out);
  not not_16 (not_16_out, in_1[0]);
  not not_17 (not_17_out, in_1[2]);
  and and_12 (and_12_out, in_1[3], not_17_out, in_1[1]);
  and and_13 (and_13_out, in_1[3], in_1[1], not_18_out);
  not not_18 (not_18_out, in_1[0]);
  not not_19 (not_19_out, in_1[3]);
  and and_14 (and_14_out, not_19_out, not_20_out);
  not not_20 (not_20_out, in_1[0]);
  not not_21 (not_21_out, in_1[2]);
  and and_15 (and_15_out, not_21_out, not_22_out);
  not not_22 (not_22_out, in_1[0]);
  and and_16 (and_16_out, in_1[3], in_1[2], not_13_out, in_1[0]);
  or or_1 (out_2[3], and_1_out, and_2_out, and_3_out, and_4_out);
  or or_2 (out_2[2], and_5_out, and_6_out, and_7_out, and_8_out);
  or or_3 (out_2[1], and_9_out, and_10_out, and_11_out, and_12_out, and_13_out);
  or or_4 (out_2[0], and_14_out, and_15_out, and_16_out);
endmodule

module test (
  input  RST,
  input  CLK,
  input  D,
  output out_4,
  output out_5
);

  wire and_1_out, and_2_out, and_3_out, not_1_out, not_2_out, or_1_out;

  not not_1 (not_1_out, D);
  and and_1 (and_1_out, CLK, not_1_out);
  and and_2 (and_2_out, CLK, D);
  not not_2 (not_2_out, RST);
  or or_1 (or_1_out, RST, and_1_out);
  and and_3 (and_3_out, and_2_out, not_2_out);
  SR_LATCH_WITH_RST sr_latch_with_rst_1 (.in_1(RST), .in_2(or_1_out), .in_3(and_3_out), .out_4(out_4), .out_5(out_5));
endmodule

module SR_LATCH_WITH_RST (
  input  in_1,
  input  in_2,
  input  in_3,
  output out_4,
  output out_5
);

  nor nor_1 (out_4, in_2, in_1, out_5);
  nor nor_2 (out_5, out_4, in_3);
endmodule
